# Fritzing sketch circuit_fritzing (saved by Fritzing 0.9.4)

parts:
  Arduino_Nano = Arduino Nano (Rev3.0)
  D1 = Rectifier Diode [part_number=1N4001 package="300 mil [THT]"]
  L1 = Solenoid
  R1 = Resistor [tolerance=±5% resistance=1k package=THT]
  Q1 = Basic FET P-Channel [package="TO220 [THT]"]

nets:
  GND: Arduino_Nano.GND, Q1.source
  N1: Arduino_Nano.D3, R1.Pin_0
  12V: Arduino_Nano.VIN, D1.cathode, L1.pin1
  N2: D1.anode, L1.pin2, Q1.drain
  N3: R1.Pin_1, Q1.gate
